# Fritzing sketch fog_wiring_diagram (saved by Fritzing 1.0.6)

parts:
  MCU1 = Raspberry Pi Zero
  Part1 = RFID-RC522-v2

nets:
  N1: MCU1.pin_1, Part1.3.3V
  N2: MCU1.pin_6, Part1.GND
  N3: MCU1.pin_19, Part1.MOSI
  N4: MCU1.pin_21, Part1.MISO
  N5: MCU1.pin_22, Part1.RST
  N6: MCU1.pin_23, Part1.SCK
  N7: MCU1.pin_24, Part1.SDA

custom parts:
  RFID-RC522-v2: A simple China made RFID-RC522 Reader; do check the pin labels, as this is a MFRC522 based clone.
