# Fritzing sketch mesh_node (saved by Fritzing 1.0.6)

parts:
  A1 = Arduino UNO R4 WiFi
  Mod1 = MQ-7 breakout

nets:
  N1: A1.Pin_7, A1.Pin_19, Mod1.VCC
  N2: A1.Pin_12, Mod1.AO
  N3: A1.Pin_25, A1.Pin_30, A1.Pin_48, Mod1.GND
  N4: A1.Pin_40, Mod1.DO

custom parts:
  Arduino UNO R4 WiFi: The Arduino UNO R4 WiFi merges the RA4M1 microprocessor from Renesas with the ESP32-S3 from Espressif, creating an all-in-one tool for makers with enhanced processing power and a diverse array of new peripherals.
  MQ-7 breakout: MQ-5 gas sensor
